// Logisim project explained.circ as structural Verilog: 10 circuits, main circuit main
module main (
  input  EN
);

  wire clock_1_out, clock_2_out, clock_3_out, clock_4_out;
  wire [3:0] Accumulator_q, B_q, Memory_Address_q;
  wire [7:0] PC_bus;
  wire [15:0] PC_ctrl;

  Clock clock_1 (.out(clock_1_out));
  Register #(.width(4)) Memory_Address (
    .D(PC_bus[3:0]), .en(PC_ctrl[3]), .Q(Memory_Address_q), .clk(clock_1_out));  // open: clr
  example8 PC (.PCMEM(PC_bus), .BUS(PC_bus[3:0]), .CTRL(PC_ctrl), .EN(EN));
  Clock clock_2 (.out(clock_2_out));
  RAM #(.addrWidth(4)) ram_1 (
    .addr(Memory_Address_q), .data(PC_bus), .sel(PC_ctrl[2]), .clk(clock_2_out), .ld(PC_ctrl[1]));  // open: clr
  Register #(.width(4)) B (.D(PC_bus[3:0]), .en(PC_ctrl[8]), .Q(B_q), .clk(clock_3_out));  // open: clr
  Clock clock_3 (.out(clock_3_out));
  Register #(.width(4)) Accumulator (
    .D(PC_bus[3:0]), .en(PC_ctrl[0]), .Q(Accumulator_q), .clk(clock_4_out));  // open: clr
  assign PC_bus[3:0] = PC_ctrl[5] ? Accumulator_q : 4'bz;  // Controlled_Buffer controlled_buffer_1
  Clock clock_4 (.out(clock_4_out));
  ALU ALU (.BUS(PC_bus[3:0]), .ALUI(PC_ctrl[6]), .BIN(B_q), .ALUO(PC_ctrl[7]), .BUS_2(PC_bus[3:0]));

  // Notes on the sheet:
  //   EN: pull=down
endmodule

module example1 (
  input  EN
);

  wire clock_1_out, demultiplexer_1_out0, demultiplexer_1_out1, demultiplexer_1_out2, demultiplexer_1_out3,
       demultiplexer_1_out4, demultiplexer_1_out5, demultiplexer_1_out6, demultiplexer_1_out7;
  wire [2:0] Counter_q;

  Counter #(.width(3), .max('h7)) Counter (.Q(Counter_q), .clk(clock_1_out));  // open: load, D, count, carry, clr
  Clock clock_1 (.out(clock_1_out));
  Demultiplexer #(.select(3), .disabled(0), .enable("false")) demultiplexer_1 (
    .out0(demultiplexer_1_out0), .out1(demultiplexer_1_out1), .out2(demultiplexer_1_out2),
    .out3(demultiplexer_1_out3), .out4(demultiplexer_1_out4), .out5(demultiplexer_1_out5),
    .out6(demultiplexer_1_out6), .out7(demultiplexer_1_out7), .in(EN), .sel(Counter_q));

  // Notes on the sheet:
  //   EN: pull=down
endmodule

module example2 (
  input  EN
);

  wire clock_1_out, clock_2_out, clock_3_out, clock_4_out, demultiplexer_1_out0, demultiplexer_1_out1,
       demultiplexer_1_out2, demultiplexer_1_out3, demultiplexer_1_out4, demultiplexer_1_out5,
       demultiplexer_1_out6, demultiplexer_1_out7;
  wire [2:0] Counter_q;
  wire [3:0] Program_Memory_Address_q;
  wire [7:0] ram_1_data;

  Register #(.width(4)) Program_Memory_Address (.Q(Program_Memory_Address_q), .clk(clock_1_out));  // open: D, en, clr
  Clock clock_1 (.out(clock_1_out));
  Clock clock_2 (.out(clock_2_out));
  Clock clock_3 (.out(clock_3_out));
  Counter #(.width(3), .max('h7)) Counter (.Q(Counter_q), .clk(clock_2_out));  // open: load, D, count, carry, clr
  RAM #(.addrWidth(4)) ram_1 (
    .addr(Program_Memory_Address_q), .data(ram_1_data), .sel(demultiplexer_1_out0), .clk(clock_3_out),
    .ld(demultiplexer_1_out0));  // open: clr
  Demultiplexer #(.select(3), .disabled(0), .enable("false")) demultiplexer_1 (
    .out0(demultiplexer_1_out0), .out1(demultiplexer_1_out1), .out2(demultiplexer_1_out2),
    .out3(demultiplexer_1_out3), .out4(demultiplexer_1_out4), .out5(demultiplexer_1_out5),
    .out6(demultiplexer_1_out6), .out7(demultiplexer_1_out7), .in(EN), .sel(Counter_q));
  Register Program_Data (.D(ram_1_data), .en(demultiplexer_1_out0), .clk(clock_4_out));  // open: Q, clr
  Clock clock_4 (.out(clock_4_out));

  // Notes on the sheet:
  //   EN: pull=down
endmodule

module example3 (
  input  EN
);

  wire clock_1_out, clock_2_out, clock_3_out, clock_4_out, demultiplexer_1_out0, demultiplexer_1_out1,
       demultiplexer_1_out2, demultiplexer_1_out3, demultiplexer_1_out4, demultiplexer_1_out5,
       demultiplexer_1_out6, demultiplexer_1_out7;
  wire [2:0] Counter_q;
  wire [3:0] adder_1_out, Program_Memory_Address_q;
  wire [7:0] ram_1_data;

  Adder #(.width(4)) adder_1 (.a(Program_Memory_Address_q), .b(4'b0001), .out(adder_1_out));  // open: cin, cout
  Register #(.width(4)) Program_Memory_Address (
    .D(adder_1_out), .en(demultiplexer_1_out1), .Q(Program_Memory_Address_q), .clk(clock_1_out));  // open: clr
  Clock clock_1 (.out(clock_1_out));
  Counter #(.width(3), .max('h7)) Counter (.Q(Counter_q), .clk(clock_2_out));  // open: load, D, count, carry, clr
  Clock clock_2 (.out(clock_2_out));
  Clock clock_3 (.out(clock_3_out));
  RAM #(.addrWidth(4)) ram_1 (
    .addr(Program_Memory_Address_q), .data(ram_1_data), .sel(demultiplexer_1_out0), .clk(clock_3_out),
    .ld(demultiplexer_1_out0));  // open: clr
  Demultiplexer #(.select(3), .disabled(0), .enable("false")) demultiplexer_1 (
    .out0(demultiplexer_1_out0), .out1(demultiplexer_1_out1), .out2(demultiplexer_1_out2),
    .out3(demultiplexer_1_out3), .out4(demultiplexer_1_out4), .out5(demultiplexer_1_out5),
    .out6(demultiplexer_1_out6), .out7(demultiplexer_1_out7), .in(EN), .sel(Counter_q));
  Register Program_Data (.D(ram_1_data), .en(demultiplexer_1_out0), .clk(clock_4_out));  // open: Q, clr
  Clock clock_4 (.out(clock_4_out));

  // Notes on the sheet:
  //   EN: pull=down
endmodule

module example4 (
  input  EN
);

  wire clock_1_out, clock_2_out, clock_3_out, clock_4_out, clock_5_out, clock_6_out, demultiplexer_1_out0,
       demultiplexer_1_out1, demultiplexer_1_out2, demultiplexer_1_out3, demultiplexer_1_out4,
       demultiplexer_1_out5, demultiplexer_1_out6, demultiplexer_1_out7;
  wire [2:0] Counter_q;
  wire [3:0] adder_1_out, bitselector_1_out, Program_Memory_Address_q;
  wire [7:0] Program_Data_q, ram_1_data;

  Adder #(.width(4)) adder_1 (.a(Program_Memory_Address_q), .b(4'b0001), .out(adder_1_out));  // open: cin, cout
  Register #(.width(4)) Program_Memory_Address (
    .D(adder_1_out), .en(demultiplexer_1_out1), .Q(Program_Memory_Address_q), .clk(clock_1_out));  // open: clr
  Clock clock_1 (.out(clock_1_out));
  Clock clock_2 (.out(clock_2_out));
  Clock clock_3 (.out(clock_3_out));
  Counter #(.width(3), .max('h7)) Counter (.Q(Counter_q), .clk(clock_2_out));  // open: load, D, count, carry, clr
  RAM #(.addrWidth(4)) ram_1 (
    .addr(Program_Memory_Address_q), .data(ram_1_data), .sel(demultiplexer_1_out0), .clk(clock_3_out),
    .ld(demultiplexer_1_out0));  // open: clr
  Demultiplexer #(.select(3), .disabled(0), .enable("false")) demultiplexer_1 (
    .out0(demultiplexer_1_out0), .out1(demultiplexer_1_out1), .out2(demultiplexer_1_out2),
    .out3(demultiplexer_1_out3), .out4(demultiplexer_1_out4), .out5(demultiplexer_1_out5),
    .out6(demultiplexer_1_out6), .out7(demultiplexer_1_out7), .in(EN), .sel(Counter_q));
  Register Program_Data (
    .D(ram_1_data), .en(demultiplexer_1_out0), .Q(Program_Data_q), .clk(clock_4_out));  // open: clr
  Clock clock_4 (.out(clock_4_out));
  BitSelector #(.group(4)) bitselector_1 (.in(Program_Data_q), .out(bitselector_1_out), .sel(demultiplexer_1_out3));
  Register #(.width(4)) Target_Memory_Address (
    .D(bitselector_1_out), .en(demultiplexer_1_out3), .clk(clock_5_out));  // open: Q, clr
  Clock clock_5 (.out(clock_5_out));
  Register #(.width(4)) Instruction_Address (
    .D(bitselector_1_out), .en(demultiplexer_1_out2), .clk(clock_6_out));  // open: Q, clr
  Clock clock_6 (.out(clock_6_out));

  // Notes on the sheet:
  //   EN: pull=down
endmodule

module example5 (
  input  EN
);

  wire clock_1_out, clock_2_out, clock_3_out, clock_4_out, clock_5_out, clock_6_out, clock_7_out,
       demultiplexer_1_out0, demultiplexer_1_out1, demultiplexer_1_out2, demultiplexer_1_out3,
       demultiplexer_1_out4, demultiplexer_1_out5, demultiplexer_1_out6, demultiplexer_1_out7;
  wire [2:0] Counter_q;
  wire [3:0] adder_1_out, bitselector_1_out, Instruction_Address_q, Program_Memory_Address_q;
  wire [7:0] Program_Data_q, ram_1_data;
  wire [15:0] register_1_q, rom_1_data;

  Adder #(.width(4)) adder_1 (.a(Program_Memory_Address_q), .b(4'b0001), .out(adder_1_out));  // open: cin, cout
  Register #(.width(4)) Program_Memory_Address (
    .D(adder_1_out), .en(demultiplexer_1_out1), .Q(Program_Memory_Address_q), .clk(clock_1_out));  // open: clr
  Clock clock_1 (.out(clock_1_out));
  Counter #(.width(3), .max('h7)) Counter (.Q(Counter_q), .clk(clock_2_out));  // open: load, D, count, carry, clr
  Clock clock_2 (.out(clock_2_out));
  Clock clock_3 (.out(clock_3_out));
  RAM #(.addrWidth(4)) ram_1 (
    .addr(Program_Memory_Address_q), .data(ram_1_data), .sel(demultiplexer_1_out0), .clk(clock_3_out),
    .ld(demultiplexer_1_out0));  // open: clr
  Demultiplexer #(.select(3), .disabled(0), .enable("false")) demultiplexer_1 (
    .out0(demultiplexer_1_out0), .out1(demultiplexer_1_out1), .out2(demultiplexer_1_out2),
    .out3(demultiplexer_1_out3), .out4(demultiplexer_1_out4), .out5(demultiplexer_1_out5),
    .out6(demultiplexer_1_out6), .out7(demultiplexer_1_out7), .in(EN), .sel(Counter_q));
  Register Program_Data (
    .D(ram_1_data), .en(demultiplexer_1_out0), .Q(Program_Data_q), .clk(clock_4_out));  // open: clr
  Clock clock_4 (.out(clock_4_out));
  BitSelector #(.group(4)) bitselector_1 (.in(Program_Data_q), .out(bitselector_1_out), .sel(demultiplexer_1_out3));
  Register #(.width(4)) Target_Memory_Address (
    .D(bitselector_1_out), .en(demultiplexer_1_out3), .clk(clock_5_out));  // open: Q, clr
  Clock clock_5 (.out(clock_5_out));
  Register #(.width(4)) Instruction_Address (
    .D(bitselector_1_out), .en(demultiplexer_1_out2), .Q(Instruction_Address_q), .clk(clock_6_out));  // open: clr
  Clock clock_6 (.out(clock_6_out));
  Register #(.width(16)) register_1 (
    .D(rom_1_data), .en(demultiplexer_1_out4), .Q(register_1_q), .clk(clock_7_out));  // open: clr
  ROM #(.addrWidth(4), .dataWidth(16)) rom_1 (
    .addr(Instruction_Address_q), .data(rom_1_data), .sel(demultiplexer_1_out4));
  Clock clock_7 (.out(clock_7_out));

  // Notes on the sheet:
  //   EN: pull=down
  //   contents of rom_1 (hex, n*v repeats v):
  //   a4e8 8bf0 ae75 1986 f4d9 6487 1f5f 17c3 c990 9270 dd1d 1bf3 b75a 1c61 1a00 7e61
endmodule

module example6 (
  input  EN
);

  wire clock_1_out, clock_2_out, clock_3_out, clock_4_out, clock_5_out, clock_6_out, clock_7_out,
       demultiplexer_1_out0, demultiplexer_1_out1, demultiplexer_1_out2, demultiplexer_1_out3,
       demultiplexer_1_out4, demultiplexer_1_out5, demultiplexer_1_out6, demultiplexer_1_out7, or_1_out;
  wire [2:0] Counter_q;
  wire [3:0] adder_1_out, adder_2_out, adder_3_out, adder_4_out, bitselector_1_out, controlled_buffer_1_out,
       Instruction_Address_q, Program_Memory_Address_q;
  wire [7:0] Program_Data_q, ram_1_data;
  wire [15:0] register_1_q, rom_1_data;

  Adder #(.width(4)) adder_1 (.a(Program_Memory_Address_q), .b(4'b0001), .out(adder_1_out));  // open: cin, cout
  Register #(.width(4)) Program_Memory_Address (
    .D(adder_1_out), .en(demultiplexer_1_out1), .Q(Program_Memory_Address_q), .clk(clock_1_out));  // open: clr
  Clock clock_1 (.out(clock_1_out));
  Clock clock_2 (.out(clock_2_out));
  Counter #(.width(3), .max('h7)) Counter (.Q(Counter_q), .clk(clock_3_out));  // open: load, D, count, carry, clr
  Clock clock_3 (.out(clock_3_out));
  RAM #(.addrWidth(4)) ram_1 (
    .addr(Program_Memory_Address_q), .data(ram_1_data), .sel(demultiplexer_1_out0), .clk(clock_2_out),
    .ld(demultiplexer_1_out0));  // open: clr
  Demultiplexer #(.select(3), .disabled(0), .enable("false")) demultiplexer_1 (
    .out0(demultiplexer_1_out0), .out1(demultiplexer_1_out1), .out2(demultiplexer_1_out2),
    .out3(demultiplexer_1_out3), .out4(demultiplexer_1_out4), .out5(demultiplexer_1_out5),
    .out6(demultiplexer_1_out6), .out7(demultiplexer_1_out7), .in(EN), .sel(Counter_q));
  Register Program_Data (
    .D(ram_1_data), .en(demultiplexer_1_out0), .Q(Program_Data_q), .clk(clock_4_out));  // open: clr
  Clock clock_4 (.out(clock_4_out));
  BitSelector #(.group(4)) bitselector_1 (.in(Program_Data_q), .out(bitselector_1_out), .sel(demultiplexer_1_out3));
  Register #(.width(4)) Target_Memory_Address (
    .D(bitselector_1_out), .en(demultiplexer_1_out3), .clk(clock_5_out));  // open: Q, clr
  Clock clock_5 (.out(clock_5_out));
  Register #(.width(4)) Instruction_Address (
    .D(bitselector_1_out), .en(demultiplexer_1_out2), .Q(Instruction_Address_q), .clk(clock_6_out));  // open: clr
  Clock clock_6 (.out(clock_6_out));
  Adder #(.width(4)) adder_2 (.a(Instruction_Address_q), .b(4'b0001), .out(adder_2_out));  // open: cin, cout
  Adder #(.width(4)) adder_3 (.a(Instruction_Address_q), .b(4'b0010), .out(adder_3_out));  // open: cin, cout
  Adder #(.width(4)) adder_4 (.a(Instruction_Address_q), .b(4'b0011), .out(adder_4_out));  // open: cin, cout
  assign controlled_buffer_1_out = demultiplexer_1_out4 ? Instruction_Address_q : 4'bz;  // Controlled_Buffer controlled_buffer_1
  assign controlled_buffer_1_out = demultiplexer_1_out5 ? adder_2_out : 4'bz;  // Controlled_Buffer controlled_buffer_2
  assign controlled_buffer_1_out = demultiplexer_1_out6 ? adder_3_out : 4'bz;  // Controlled_Buffer controlled_buffer_3
  assign controlled_buffer_1_out = demultiplexer_1_out7 ? adder_4_out : 4'bz;  // Controlled_Buffer controlled_buffer_4
  or or_1 (or_1_out, demultiplexer_1_out4, demultiplexer_1_out5, demultiplexer_1_out6, demultiplexer_1_out7);
  ROM #(.addrWidth(4), .dataWidth(16)) rom_1 (.addr(controlled_buffer_1_out), .data(rom_1_data), .sel(or_1_out));
  Register #(.width(16)) register_1 (.D(rom_1_data), .en(or_1_out), .Q(register_1_q), .clk(clock_7_out));  // open: clr
  Clock clock_7 (.out(clock_7_out));

  // Notes on the sheet:
  //   EN: pull=down
  //   contents of rom_1 (hex, n*v repeats v):
  //   a4e8 8bf0 ae75 1986 f4d9 6487 1f5f 17c3 c990 9270 dd1d 1bf3 b75a 1c61 1a00 7e61
endmodule

module example7 (
  input  EN
);

  wire clock_1_out, clock_2_out, clock_3_out, clock_4_out, clock_5_out, clock_6_out, clock_7_out,
       clock_8_out, clock_9_out, demultiplexer_1_out2, demultiplexer_1_out3, demultiplexer_1_out4,
       demultiplexer_1_out5, demultiplexer_1_out6, demultiplexer_1_out7, or_1_out;
  wire [2:0] Counter_q;
  wire [3:0] adder_1_out, adder_2_out, adder_3_out, adder_4_out, bitselector_1_out, controlled_buffer_1_out,
       controlled_buffer_3_out, Instruction_Address_q, Memory_Address_q, Program_Memory_Address_q,
       Target_Memory_Address_q;
  wire [7:0] Program_Data_q;
  wire [7:4] ram_1_data;
  wire [15:0] or_2_out, pull_resistor_1_node, register_1_q, rom_1_data;

  Adder #(.width(4)) adder_1 (.a(Program_Memory_Address_q), .b(4'b0001), .out(adder_1_out));  // open: cin, cout
  Register #(.width(4)) Program_Memory_Address (
    .en(pull_resistor_1_node[2]), .Q(Program_Memory_Address_q), .clk(clock_1_out));  // open: D, clr
  Clock clock_1 (.out(clock_1_out));
  Clock clock_2 (.out(clock_2_out));
  assign controlled_buffer_1_out = pull_resistor_1_node[3] ? Program_Memory_Address_q : 4'bz;  // Controlled_Buffer controlled_buffer_1
  Register #(.width(4)) Memory_Address (
    .D(controlled_buffer_1_out), .en(or_2_out[3]), .Q(Memory_Address_q), .clk(clock_2_out));  // open: clr
  Counter #(.width(3), .max('h7)) Counter (.Q(Counter_q), .clk(clock_3_out));  // open: load, D, count, carry, clr
  Clock clock_3 (.out(clock_3_out));
  Clock clock_4 (.out(clock_4_out));
  Demultiplexer #(.select(3), .disabled(0), .enable("false")) demultiplexer_1 (
    .out0(pull_resistor_1_node[3]), .out1(pull_resistor_1_node[2]), .out2(demultiplexer_1_out2),
    .out3(demultiplexer_1_out3), .out4(demultiplexer_1_out4), .out5(demultiplexer_1_out5),
    .out6(demultiplexer_1_out6), .out7(demultiplexer_1_out7), .in(EN), .sel(Counter_q));
  RAM #(.addrWidth(4)) ram_1 (
    .addr(Memory_Address_q), .data({ram_1_data, controlled_buffer_1_out}), .sel(or_2_out[2]),
    .clk(clock_4_out), .ld(or_2_out[1]));  // open: clr
  Register Program_Data (
    .D({ram_1_data, controlled_buffer_1_out}), .en(pull_resistor_1_node[2]), .Q(Program_Data_q),
    .clk(clock_5_out));  // open: clr
  Clock clock_5 (.out(clock_5_out));
  BitSelector #(.group(4)) bitselector_1 (.in(Program_Data_q), .out(bitselector_1_out), .sel(demultiplexer_1_out3));
  Register #(.width(4)) Target_Memory_Address (
    .D(bitselector_1_out), .en(demultiplexer_1_out3), .Q(Target_Memory_Address_q), .clk(clock_6_out));  // open: clr
  Clock clock_6 (.out(clock_6_out));
  Register #(.width(4)) Instruction_Address (
    .D(bitselector_1_out), .en(demultiplexer_1_out2), .Q(Instruction_Address_q), .clk(clock_7_out));  // open: clr
  Clock clock_7 (.out(clock_7_out));
  assign controlled_buffer_1_out = or_2_out[4] ? Target_Memory_Address_q : 4'bz;  // Controlled_Buffer controlled_buffer_2
  Adder #(.width(4)) adder_2 (.a(Instruction_Address_q), .b(4'b0001), .out(adder_2_out));  // open: cin, cout
  Adder #(.width(4)) adder_3 (.a(Instruction_Address_q), .b(4'b0010), .out(adder_3_out));  // open: cin, cout
  Adder #(.width(4)) adder_4 (.a(Instruction_Address_q), .b(4'b0011), .out(adder_4_out));  // open: cin, cout
  Clock clock_8 (.out(clock_8_out));
  assign controlled_buffer_3_out = demultiplexer_1_out4 ? Instruction_Address_q : 4'bz;  // Controlled_Buffer controlled_buffer_3
  assign controlled_buffer_3_out = demultiplexer_1_out5 ? adder_2_out : 4'bz;  // Controlled_Buffer controlled_buffer_4
  assign controlled_buffer_3_out = demultiplexer_1_out6 ? adder_3_out : 4'bz;  // Controlled_Buffer controlled_buffer_5
  assign controlled_buffer_3_out = demultiplexer_1_out7 ? adder_4_out : 4'bz;  // Controlled_Buffer controlled_buffer_6
  Register #(.width(4)) Accumulator (.D(controlled_buffer_1_out), .en(or_2_out[0]), .clk(clock_8_out));  // open: Q, clr
  or or_1 (or_1_out, demultiplexer_1_out4, demultiplexer_1_out5, demultiplexer_1_out6, demultiplexer_1_out7);
  ROM #(.addrWidth(4), .dataWidth(16)) rom_1 (.addr(controlled_buffer_3_out), .data(rom_1_data), .sel(or_1_out));
  assign or_2_out = register_1_q | {pull_resistor_1_node[15:2], pull_resistor_1_node[2], pull_resistor_1_node[0]};  // OR_Gate or_2, 16 bits wide
  Register #(.width(16)) register_1 (.D(rom_1_data), .en(or_1_out), .Q(register_1_q), .clk(clock_9_out));  // open: clr
  Clock clock_9 (.out(clock_9_out));
  Pull_Resistor pull_resistor_1 (.node({pull_resistor_1_node[15:2], pull_resistor_1_node[2], pull_resistor_1_node[0]}));

  // Notes on the sheet:
  //   EN: pull=down
  //   contents of rom_1 (hex, n*v repeats v):
  //   4*0 18 7
endmodule

module example8 (
  input  [7:0] PCMEM,
  input  EN,
  output [3:0] BUS,
  output [15:0] CTRL
);

  wire clock_1_out, clock_2_out, clock_3_out, clock_4_out, clock_5_out, demultiplexer_1_out2,
       demultiplexer_1_out3, demultiplexer_1_out4, demultiplexer_1_out5, demultiplexer_1_out6,
       demultiplexer_1_out7, or_1_out;
  wire [2:0] Counter_q;
  wire [3:0] adder_1_out, adder_2_out, bitselector_1_out, controlled_buffer_3_out, Instruction_Address_q,
       Program_Memory_Address_q, Target_Memory_Address_q;
  wire [7:0] Program_Data_q;
  wire [15:0] pull_resistor_1_node, pull_resistor_2_node, rom_1_data;

  Adder #(.width(4)) adder_1 (.a(Program_Memory_Address_q), .b(4'b0001), .out(adder_1_out));  // open: cin, cout
  Register #(.width(4)) Program_Memory_Address (
    .D(adder_1_out), .en(pull_resistor_2_node[2]), .Q(Program_Memory_Address_q), .clk(clock_1_out));  // open: clr
  Clock clock_1 (.out(clock_1_out));
  assign BUS = pull_resistor_2_node[3] ? Program_Memory_Address_q : 4'bz;  // Controlled_Buffer controlled_buffer_1
  Counter #(.width(3), .max('h7)) Counter (.Q(Counter_q), .clk(clock_2_out));  // open: load, D, count, carry, clr
  Clock clock_2 (.out(clock_2_out));
  Demultiplexer #(.select(3), .disabled(0), .enable("false")) demultiplexer_1 (
    .out0(pull_resistor_2_node[3]), .out1(pull_resistor_2_node[2]), .out2(demultiplexer_1_out2),
    .out3(demultiplexer_1_out3), .out4(demultiplexer_1_out4), .out5(demultiplexer_1_out5),
    .out6(demultiplexer_1_out6), .out7(demultiplexer_1_out7), .in(EN), .sel(Counter_q));
  Register Program_Data (.D(PCMEM), .en(pull_resistor_2_node[2]), .Q(Program_Data_q), .clk(clock_3_out));  // open: clr
  Clock clock_3 (.out(clock_3_out));
  BitSelector #(.group(4)) bitselector_1 (.in(Program_Data_q), .out(bitselector_1_out), .sel(demultiplexer_1_out3));
  Register #(.width(4)) Target_Memory_Address (
    .D(bitselector_1_out), .en(demultiplexer_1_out3), .Q(Target_Memory_Address_q), .clk(clock_4_out));  // open: clr
  Clock clock_4 (.out(clock_4_out));
  Register #(.width(4)) Instruction_Address (
    .D(bitselector_1_out), .en(demultiplexer_1_out2), .Q(Instruction_Address_q), .clk(clock_5_out));  // open: clr
  Clock clock_5 (.out(clock_5_out));
  assign BUS = CTRL[4] ? Target_Memory_Address_q : 4'bz;  // Controlled_Buffer controlled_buffer_2
  Adder #(.width(4)) adder_2 (.a(Instruction_Address_q), .b(4'b0001), .out(adder_2_out));  // open: cin, cout
  assign controlled_buffer_3_out = demultiplexer_1_out4 ? Instruction_Address_q : 4'bz;  // Controlled_Buffer controlled_buffer_3
  assign controlled_buffer_3_out = demultiplexer_1_out5 ? adder_2_out : 4'bz;  // Controlled_Buffer controlled_buffer_4
  or or_1 (or_1_out, demultiplexer_1_out4, demultiplexer_1_out5, demultiplexer_1_out6);
  ROM #(.addrWidth(4), .dataWidth(16)) rom_1 (.addr(controlled_buffer_3_out), .data(rom_1_data), .sel(or_1_out));
  Pull_Resistor pull_resistor_1 (.node(pull_resistor_1_node));
  assign pull_resistor_1_node = or_1_out ? rom_1_data : 16'bz;  // Controlled_Buffer controlled_buffer_5
  Pull_Resistor pull_resistor_2 (.node({pull_resistor_2_node[15:2], pull_resistor_2_node[2], pull_resistor_2_node[0]}));
  assign CTRL = pull_resistor_1_node | {pull_resistor_2_node[15:2], pull_resistor_2_node[2], pull_resistor_2_node[0]};  // OR_Gate or_2, 16 bits wide

  // Notes on the sheet:
  //   BUS: pull=down
  //   EN: pull=down
  //   PCMEM: pull=down
  //   CTRL: pull=down
  //   contents of rom_1 (hex, n*v repeats v):
  //   0 0 18 7 18 106 60 81
endmodule

module ALU (
  input  [3:0] BUS,
  input  ALUI,
  input  [3:0] BIN,
  input  ALUO,
  output [3:0] BUS_2
);

  wire clock_1_out;
  wire [3:0] adder_1_out, register_1_q;

  Clock clock_1 (.out(clock_1_out));
  Register #(.width(4)) register_1 (.D(BUS), .en(ALUI), .Q(register_1_q), .clk(clock_1_out));  // open: clr
  assign BUS_2 = ALUO ? adder_1_out : 4'bz;  // Controlled_Buffer controlled_buffer_1
  Adder #(.width(4)) adder_1 (.a(register_1_q), .b(BIN), .out(adder_1_out));  // open: cin, cout

  // Notes on the sheet:
  //   ALUI: pull=down
  //   BUS_2: pull=down
  //   BUS: pull=down
  //   BIN: pull=down
  //   ALUO: pull=down
endmodule
